# Fritzing sketch masterFritzing (saved by Fritzing 0.9.3b)
breadboards: 1

parts:
  S3 = Momentary Switch [package=tactile-pth]
  U2 = POT [package=pot_alpha_rv16af-20]
  Componente1 = Arduino Uno (Rev3)
  Componente2 = NRF24L01+ Breakout Board

nets:
  GND: S3.3, U2.E, Componente1.GND, Componente2.GND
  N1: U2.A, Componente1.5V
  N2: U2.S, Componente1.A0
  N3: Componente1.D9_PWM, Componente2.CE
  N4: Componente1.D10_PWM/SS, Componente2.CS
  N5: Componente1.D11_PWM/MOSI, Componente2.MOSI
  N6: Componente1.D12/MISO, Componente2.MISO
  N7: Componente1.D13/SCK, Componente2.SCK
  3V3: Componente1.3V3, Componente2.VCC
