# Fritzing sketch slaveFritzing (saved by Fritzing 0.9.3b)
breadboards: 1

parts:
  Componente1 = Arduino Uno (Rev3)
  Componente2 = NRF24L01+ Breakout Board
  LED1 = smd LED [color="Red (633nm)" package="0603 [SMD]"]
  J1 = Basic Servo

nets:
  N1: Componente1.D9_PWM, Componente2.CE
  N2: Componente1.D10_PWM/SS, Componente2.CS
  N3: Componente1.D11_PWM/MOSI, Componente2.MOSI
  N4: Componente1.D12/MISO, Componente2.MISO
  N5: Componente1.D13/SCK, Componente2.SCK
  GND: Componente1.GND, Componente2.GND, LED1.cathode, J1.gnd
  N6: Componente1.D3_PWM, LED1.anode
  N7: Componente1.D5_PWM, J1.pulse
  3V3: Componente1.3V3, Componente2.VCC
  5V: Componente1.5V, J1.vcc
